# Fritzing sketch FourthProject (saved by Fritzing 0.9.9b)
breadboards: 2

parts:
  Mod1 = Raspberry Pi Pico
  R1 = Resistor [tolerance=±5% power=0.25 resistance=10k package=THT]
  LED1 = LED - 3mm [color="Red (633nm)" current=0.030 package="3 mm [THT]"]
  S1 = Pushbutton [package="[THT]"]
  Display1 = LCD screen 16x2 IIC [part_number=101290]
  Driver1 = 28BYJ-48 Driver Module [part_number=ULN2003 package=THT]
  SM1 = 28BYJ-48 Stepper Motor [part_number=28BYJ-48]
  YwRobot_Power_Supply1 = YwRobot Breadboard Power Supply [part_number=545043]

nets:
  N1: Mod1.pin_1, LED1.anode
  N2: Mod1.pin_2, R1.Pin_1, S1.Pin_3, S1.Pin_4
  N3: Mod1.pin_3, Mod1.pin_8, LED1.cathode, S1.Pin_1, S1.Pin_2, Display1.GND, Driver1.IN3
  N4: Mod1.pin_5, Display1.SCL
  N5: Mod1.pin_6, Driver1.IN1
  N6: Mod1.pin_7, Driver1.IN2
  N7: Mod1.pin_9, Driver1.IN4
  N8: Mod1.pin_36, R1.Pin_0, Display1.VCC
  N9: Driver1.GND, YwRobot_Power_Supply1.GND#11
  N10: Driver1.Vmotor, YwRobot_Power_Supply1.VCC#5
  N11: Driver1.blue-pin, SM1.blue-pin
  N12: Driver1.pink-pin, SM1.pink-pin
  N13: Driver1.yellow-pin, SM1.yellow-pin
  N14: Driver1.orange-pin, SM1.orange-pin
  N15: Driver1.red-pin, SM1.red-pin

custom parts:
  Raspberry Pi Pico: Raspberry Pi Pico. Based around the RP2040 microcontroller the Pico is a low cost microcontroller device bringing Raspberry Pi quality, cost, and easy of use to the microcontroller space. Jan 2021, Split part in to two versions: tht (this one) and SMD. This one will drill holes for a .1 in header in pcb to allow plugging in the module as well as providing pads to solder the module to the top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
  LCD screen 16x2 IIC: LCD screen with HD44780 controller enables showing text, symbols, value or anything else that comes from Croduino/Arduino. It is capable of showing 16 symbols in two lines and therefore can be used in many projects that need to send clearly visible and legible output information.. • Color of symbols: White • Backlight: Blue • Dimensions: 80 x 36 x 12 mm • Screen dimensions: 64.5 x 16 mm •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
  28BYJ-48 Driver Module: ULN2003 Driver Module for the 28BYJ-48 Unipolar Stepper Motor LED A - Blue wire - Bottom coil left LED B - Pink wire - Top coil left LED C - Yellow wire - Bottom coil right LED D - Orange wire - Top coil right Common rail - red Connector pins: blue - pink - yellow - orange - red Control pins - IN1 to IN4 Power pins - GND & Vmotor (5-12V) On/Off jumper (if removed, power to motor is cut).
  28BYJ-48 Stepper Motor: Unipolar Stepper Motor 28BYJ-48 Top coil - pink & orange Bottom coil - blue & yellow Common rail - red Connector pins: blue - pink - yellow - orange - red
  YwRobot Breadboard Power Supply: The YwRobot Breadboard Power Supply (MB-V2) has two power rails; they can be 5V or 3V3. Power to the module can be provided through the female USB socket or through the A10 (female) 2.1mm power jack.
