# Fritzing sketch ThirdProject (saved by Fritzing 0.9.9b)
breadboards: 1

parts:
  Mod1 = Raspberry Pi Pico
  R1 = Resistor [tolerance=±5% power=0.25 resistance=10k package=THT]
  LED1 = LED - 3mm [color="Red (633nm)" current=0.030 package="3 mm [THT]"]
  S1 = Pushbutton [package="[THT]"]
  Display1 = LCD screen 16x2 IIC [part_number=101290]

nets:
  N1: Mod1.pin_1, LED1.anode
  N2: Mod1.pin_2, R1.Pin_1, S1.Pin_3, S1.Pin_4
  N3: Mod1.pin_3, LED1.cathode, S1.Pin_1, S1.Pin_2, Display1.GND
  N4: Mod1.pin_4, Display1.SDA
  N5: Mod1.pin_5, Display1.SCL
  N6: Mod1.pin_36, R1.Pin_0, Display1.VCC

custom parts:
  Raspberry Pi Pico: Raspberry Pi Pico. Based around the RP2040 microcontroller the Pico is a low cost microcontroller device bringing Raspberry Pi quality, cost, and easy of use to the microcontroller space. Jan 2021, Split part in to two versions: tht (this one) and SMD. This one will drill holes for a .1 in header in pcb to allow plugging in the module as well as providing pads to solder the module to the top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
  LCD screen 16x2 IIC: LCD screen with HD44780 controller enables showing text, symbols, value or anything else that comes from Croduino/Arduino. It is capable of showing 16 symbols in two lines and therefore can be used in many projects that need to send clearly visible and legible output information.. • Color of symbols: White • Backlight: Blue • Dimensions: 80 x 36 x 12 mm • Screen dimensions: 64.5 x 16 mm •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
